# Fritzing sketch girlfriendbox (saved by Fritzing 0.9.3b)

parts:
  U1 = DC-DC 2-24V Step Up Booster [package=THT]
  U2 = LIPO-1000mAh [package=lipo-1000]
  TP1 = TP4056 [chip_label=TP4056 package="DIP (Dual Inline) [THT]"]
  S1 = Toggle Switch [package=THT]
  Part1 = Arduino Nano (Rev3.0)
  Part2 = LCD1602-I2C
  ZS-042_RTC1 = ZS-042 RTC Module
  S2 = Momentary Switch [package=ksa_sealed_tac_switch]
  S3 = Momentary Switch [package=ksa_sealed_tac_switch]
  S4 = Momentary Switch [package=ksa_sealed_tac_switch]

nets:
  N1: U1.pin1, Part1.VIN
  GND: U1.pin2, Part1.GND, Part2.GND, ZS-042_RTC1.GND, S2.3, S3.3, S4.3
  N2: U1.pin3, S1.L1
  N3: U1.pin4, TP1.pin6
  N4: U2.+, U2.-, TP1.pin4, TP1.pin5
  N5: TP1.pin3, S1.COM
  N6: Part1.D2, S3.2
  N7: Part1.D3, S2.2
  N8: Part1.D4, S4.2
  VCC: Part1.5V, Part2.VCC, ZS-042_RTC1.VCC
  N9: Part1.A5, Part2.SCL, ZS-042_RTC1.SCL
  N10: Part1.A4, Part2.SDA, ZS-042_RTC1.SDA

custom parts:
  DC-DC 2-24V Step Up Booster: Convertisseur DC-DC 2-24V 2A
  TP4056: A DIP stand-in part for whatever IC you want. With 6 pins on a 300mil dual inline package (DIP) footprint.
  LCD1602-I2C: A standard character display, usually with 2x16 characters. Comes in many colors with LCM1602 IIC attached.
